# Fritzing sketch rain_drop_sensor_sketch (saved by Fritzing 0.8.7b)
breadboards: 1

parts:
  Composant1 = Arduino Nano (Rev3.0)
  S2 = Toggle Switch [package=THT]
  Buzzer = SPEAKER [package=pcb_mount_speaker]
  part = TRANSISTOR_NPN [part_number=2N2222 package=to-92-ammo]
  part_2 = Resistor [tolerance=±5% resistance=2.2k package=THT]
  BAT1 = BC9VPC [package=bc9vpc]
  part_3 = Resistor [tolerance=±5% resistance=1M package=THT]

nets:
  N1: Composant1.GND, part.C, BAT1.V+, part_3.Pin_0
  N2: Composant1.D8, part_2.Pin_1
  N3: Composant1.VIN, S2.L2
  N4: Composant1.5V, Buzzer.-
  N5: Composant1.A0, part_3.Pin_1
  N6: S2.COM, BAT1.V-
  N7: Buzzer.+, part.E
  N8: part.B, part_2.Pin_0

notes:
  Water sensor
